// Logisim project ReduxV.circ as structural Verilog: 6 circuits, main circuit main
module main (
);

  wire Branch, BranchEZero, CLK, Jump, Mem_en, not_1_out, Reg_en, Tipo_I, Wb_Source, Zero;
  wire [1:0] imm, intruct_1_r1, intruct_1_r2, multiplexer_3_out;
  wire [2:0] Ula_Op;
  wire [3:0] intruct_1_imm, intruct_1_opcode, multiplexer_4_out;
  wire [7:0] bit_extender_1_out, bit_extender_2_out, dual_port_ram_2_data, Inf_b, Inst, Jump_ad, Mem_Inst,
       multiplexer_1_out, multiplexer_2_out, multiplexer_6_out, PC_q, regbank_1_inf_a, shifter_1_out,
       ula_1_ula_out;
  wire [10:0] Control_mem_data;

  // Probe on multiplexer_1_out
  Multiplexer #(.width(8)) multiplexer_1 (.in0(multiplexer_2_out), .in1(Jump_ad), .out(multiplexer_1_out), .sel(Jump));
  Register PC (.D(multiplexer_1_out), .en(1'b1), .clk(not_1_out), .Q(PC_q));  // open: clr
  not not_1 (not_1_out, CLK);
  Multiplexer #(.width(8)) multiplexer_2 (.in0(Mem_Inst), .in1(Inf_b), .out(multiplexer_2_out), .sel(BranchEZero));
  Adder adder_1 (.a(8'h1), .b(PC_q), .out(Mem_Inst), .cin(1'b0));  // open: cout
  Dual_port_RAM dual_port_ram_1 ();  // open: addr, pc, d, w, instr, data
  Clock #(.highDuration(2), .lowDuration(2)) clock_1 (.out(CLK));
  intruct intruct_1 (.Inst(Inst), .opcode(intruct_1_opcode), .R1(intruct_1_r1), .R2(intruct_1_r2), .imm(intruct_1_imm));
  ROM #(.addrWidth(4), .dataWidth(11)) Control_mem (.addr(intruct_1_opcode), .data(Control_mem_data));
  Multiplexer #(.width(2)) multiplexer_3 (.in0(intruct_1_r1), .in1(2'b00), .out(multiplexer_3_out), .sel(Tipo_I));
  Multiplexer #(.width(4)) multiplexer_4 (.in0(intruct_1_imm), .in1(4'b0000), .out(multiplexer_4_out), .sel(Branch));
  assign bit_extender_1_out = {{4{intruct_1_imm[3]}}, intruct_1_imm};  // Bit_Extender bit_extender_1
  assign bit_extender_2_out = {{4{1'b0}}, multiplexer_4_out};  // Bit_Extender bit_extender_2
  RegBank regbank_1 (
    .WriteBack(multiplexer_6_out), .Ra(multiplexer_3_out), .Rb(intruct_1_r2), .WE(Reg_en), .CLK(CLK),
    .Inf_a(regbank_1_inf_a), .Inf_b(Inf_b));
  Shifter shifter_1 (.in(bit_extender_2_out), .\dist (3'b100), .out(shifter_1_out));
  Multiplexer #(.select(2), .width(8)) multiplexer_5 (
    .in0(Inf_b), .in1(bit_extender_1_out), .in2(bit_extender_2_out), .in3(shifter_1_out), .out(Jump_ad),
    .sel(imm));
  Multiplexer #(.width(8)) multiplexer_6 (
    .in0(dual_port_ram_2_data), .in1(ula_1_ula_out), .out(multiplexer_6_out), .sel(Wb_Source));
  Controle controle_1 (
    .opcode(Control_mem_data), .imm(imm), .Mem_en(Mem_en), .Tipo_I(Tipo_I), .Reg_en(Reg_en), .Branch(Branch),
    .Jump(Jump), .Writeback(Wb_Source), .Ula_op(Ula_Op));
  ULA ula_1 (.Ula_op(Ula_Op), .Ra(regbank_1_inf_a), .Rb(Jump_ad), .zero(Zero), .ULA_out(ula_1_ula_out));
  and and_1 (BranchEZero, Branch, Zero);
  // Probe on Inst
  Dual_port_RAM dual_port_ram_2 (
    .addr(Inf_b), .pc(Mem_Inst), .d(regbank_1_inf_a), .w(Mem_en), .instr(Inst), .data(dual_port_ram_2_data));

  // Notes on the sheet:
  //   contents of Control_mem (hex, n*v repeats v):
  //   421 290 40 100 2c8 4c8 6c8 0 4f 4c 4d 4e 48 49 4a 4b
endmodule

module RegBank (
  input  [7:0] WriteBack,
  input  [1:0] Ra,
  input  [1:0] Rb,
  input  WE,
  input  CLK,
  output [7:0] Inf_a,
  output [7:0] Inf_b
);

  wire and_1_out, demultiplexer_2_out0, demultiplexer_2_out1, demultiplexer_2_out2, demultiplexer_2_out3;
  wire [7:0] demultiplexer_1_out0, demultiplexer_1_out1, demultiplexer_1_out2, demultiplexer_1_out3, R0, R1,
       R2, R3;

  Clock #(.highDuration(2), .lowDuration(2)) clock_1 ();  // open: out
  Demultiplexer #(.select(2), .width(8)) demultiplexer_1 (
    .out0(demultiplexer_1_out0), .out1(demultiplexer_1_out1), .out2(demultiplexer_1_out2),
    .out3(demultiplexer_1_out3), .in(WriteBack), .sel(Ra));
  and and_1 (and_1_out, WE, CLK);
  Demultiplexer #(.select(2)) demultiplexer_2 (
    .out0(demultiplexer_2_out0), .out1(demultiplexer_2_out1), .out2(demultiplexer_2_out2),
    .out3(demultiplexer_2_out3), .in(and_1_out), .sel(Ra));
  Register u_R0 (.D(demultiplexer_1_out0), .en(demultiplexer_2_out0), .clk(CLK), .Q(R0));  // open: clr
  Register u_R1 (.D(demultiplexer_1_out1), .en(demultiplexer_2_out1), .clk(CLK), .Q(R1));  // open: clr
  Register u_R2 (.D(demultiplexer_1_out2), .en(demultiplexer_2_out2), .clk(CLK), .Q(R2));  // open: clr
  Register u_R3 (.D(demultiplexer_1_out3), .en(demultiplexer_2_out3), .clk(CLK), .Q(R3));  // open: clr
  Multiplexer #(.select(2), .width(8)) multiplexer_1 (.in0(R0), .in1(R1), .in2(R2), .in3(R3), .out(Inf_a), .sel(Ra));
  Multiplexer #(.select(2), .width(8)) multiplexer_2 (.in0(R0), .in1(R1), .in2(R2), .in3(R3), .out(Inf_b), .sel(Rb));
endmodule

module intruct (
  input  [7:0] Inst,
  output [3:0] opcode,
  output [1:0] R1,
  output [1:0] R2,
  output [3:0] imm
);


  assign imm = Inst[3:0];
  assign opcode = Inst[7:4];
  assign R1 = Inst[1:0];
  assign R2 = Inst[3:2];
endmodule

module ULA (
  input  [2:0] Ula_op,
  input  [7:0] Ra,
  input  [7:0] Rb,
  output zero,
  output [7:0] ULA_out
);

  wire adder_1_cout, or_4_out, subtractor_1_bout;
  wire [2:0] or_2_out;
  wire [2:2] or_1_out;
  wire [7:0] adder_1_out, and_1_out, not_1_out, or_3_out, shifter_1_out, shifter_2_out, subtractor_1_out,
       xor_1_out;

  or or_1 (or_1_out[2], Rb[3], Rb[4], Rb[5], Rb[6], Rb[7]);
  assign or_2_out = {3{or_1_out[2]}} | Rb[2:0];  // OR_Gate or_2, 3 bits wide
  Adder adder_1 (.a(Ra), .b(Rb), .out(adder_1_out), .cin(1'b0), .cout(adder_1_cout));
  // NoConnect on adder_1_cout
  Subtractor subtractor_1 (.a(Ra), .b(Rb), .out(subtractor_1_out), .bin(1'b0), .bout(subtractor_1_bout));
  // NoConnect on subtractor_1_bout
  Shifter shifter_1 (.in(Ra), .\dist (or_2_out), .out(shifter_1_out));
  Shifter #(.shift("lr")) shifter_2 (.in(Ra), .\dist (or_2_out), .out(shifter_2_out));
  assign and_1_out = Ra & Rb;  // AND_Gate and_1, 8 bits wide
  assign or_3_out = Ra | Rb;  // OR_Gate or_3, 8 bits wide
  assign xor_1_out = Ra ^ Rb;  // XOR_Gate xor_1, 8 bits wide
  assign not_1_out = ~Rb;  // NOT_Gate not_1, 8 bits wide
  Multiplexer #(.select(3), .width(8)) multiplexer_1 (
    .in0(adder_1_out), .in1(subtractor_1_out), .in2(shifter_1_out), .in3(shifter_2_out), .in4(and_1_out),
    .in5(or_3_out), .in6(xor_1_out), .in7(not_1_out), .out(ULA_out), .sel(Ula_op));
  or or_4 (or_4_out, subtractor_1_out[0], subtractor_1_out[1], subtractor_1_out[2], subtractor_1_out[3], subtractor_1_out[4], subtractor_1_out[5], subtractor_1_out[6], subtractor_1_out[7]);
  not not_2 (zero, or_4_out);
endmodule

module Dual_port_RAM (
  input  [7:0] addr,
  input  [7:0] pc,
  input  [7:0] d,
  input  w,
  output [7:0] instr,
  output [7:0] data
);

  wire clock_1_out, or_1_out;
  wire [7:0] multiplexer_1_out;

  Clock #(.highDuration(2), .lowDuration(2)) clock_1 (.out(clock_1_out));
  or or_1 (or_1_out, w, clock_1_out);
  Multiplexer #(.width(8)) multiplexer_1 (.in0(addr), .in1(pc), .out(multiplexer_1_out), .sel(clock_1_out));
  RAM #(.asyncread("true")) ram_1 (
    .addr(multiplexer_1_out), .we(or_1_out), .oe(1'b1), .clk(clock_1_out), .din(d), .dout(data));
  Register #(.trigger("falling")) pcbuf (.D(data), .en(1'b1), .clk(clock_1_out), .Q(instr));  // open: clr
endmodule

module Controle (
  input  [10:0] opcode,
  output [1:0] imm,
  output Mem_en,
  output Tipo_I,
  output Reg_en,
  output Branch,
  output Jump,
  output Writeback,
  output [2:0] Ula_op
);


  assign Branch = opcode[5];
  assign imm = opcode[10:9];
  assign Jump = opcode[4];
  assign Mem_en = opcode[8];
  assign Reg_en = opcode[6];
  assign Tipo_I = opcode[7];
  assign Ula_op = opcode[2:0];
  assign Writeback = opcode[3];
endmodule
